# Fritzing sketch board vm88 (saved by Fritzing 0.9.3b)
circuit board: 6.80438cm x 8.01463cm
circuit board: 8.46667cm x 5.64444cm

parts:
  T1 = LM35 Temperature Sensor [package="TO92 [THT]"]
  T2 = LM35 Temperature Sensor [package="TO92 [THT]"]
  T4 = LM35 Temperature Sensor [package="TO92 [THT]"]
  T5 = LM35 Temperature Sensor [package="TO92 [THT]"]
  T6 = LM35 Temperature Sensor [package="TO92 [THT]"]
  T7 = LM35 Temperature Sensor [package="TO92 [THT]"]
  T8 = LM35 Temperature Sensor [package="TO92 [THT]"]
  T10 = LM35 Temperature Sensor [package="TO92 [THT]"]
  T11 = LM35 Temperature Sensor [package="TO92 [THT]"]
  R1 = Resistor [tolerance=±5% resistance=220 package=THT]
  R3 = Resistor [tolerance=±5% resistance=220 package=THT]
  R4 = Resistor [tolerance=±5% resistance=220 package=THT]
  R8 = Resistor [tolerance=±5% resistance=220 package=THT]
  R9 = Resistor [tolerance=±5% resistance=220 package=THT]
  R10 = Resistor [tolerance=±5% resistance=220 package=THT]
  R11 = Resistor [tolerance=±5% resistance=220 package=THT]
  R12 = Resistor [tolerance=±5% resistance=220 package=THT]
  R13 = Resistor [tolerance=±5% resistance=220 package=THT]
  R14 = Resistor [tolerance=±5% resistance=220 package=THT]
  R15 = Resistor [tolerance=±5% resistance=220 package=THT]
  R16 = Resistor [tolerance=±5% resistance=220 package=THT]
  R17 = Resistor [tolerance=±5% resistance=220 package=THT]
  R18 = Resistor [tolerance=±5% resistance=220 package=THT]
  R19 = Resistor [tolerance=±5% resistance=220 package=THT]
  R21 = Resistor [tolerance=±5% resistance=220 package=THT]
  Часть2 = Bluetooth HC-05 Macho
  Q1 = NPN-Transistor [package="TO92 [THT]"]
  Q2 = NPN-Transistor [package="TO92 [THT]"]
  Q3 = NPN-Transistor [package="TO92 [THT]"]
  Q4 = NPN-Transistor [package="TO92 [THT]"]
  Q5 = NPN-Transistor [package="TO92 [THT]"]
  Q6 = NPN-Transistor [package="TO92 [THT]"]
  T9 = LM35 Temperature Sensor [package="TO92 [THT]"]
  Pad3 = Pad [width=2.6909146198830407 height=2.2971002456140357 connect=center]
  Pad4 = Pad [width=2.8581846161484794 height=2.6698012828151487 connect=center]
  Pad5 = Pad [width=2.7067618098928712 height=2.1406198853588978 connect=center]
  Pad6 = Pad [width=2.9430967356682807 height=2.3536616714875067 connect=center]
  Часть1 = Arduino Nano (Rev3.0)

nets:
  N1: T1.Vout, R4.Pin_1
  GND: T1.GND, T4.GND, Q1.C, Q2.C, Q3.C, Q4.C, Q5.C, Q6.C, Pad4.pad
  N2: T2.Vout, R19.Pin_1
  GND_2: T2.GND, T5.GND, T6.GND, T7.GND, T8.GND, T10.GND, T11.GND, T9.GND, Pad3.pad
  N3: T4.Vout, R1.Pin_1
  N4: T5.Vout, R13.Pin_1
  N5: T6.Vout, R14.Pin_1
  N6: T7.Vout, R16.Pin_1
  N7: T8.Vout, R17.Pin_1
  N8: T10.Vout, R18.Pin_1
  N9: T11.Vout, R12.Pin_1
  N10: R1.Pin_0, Часть1.A3
  N11: R3.Pin_0, Часть1.A5
  N12: R3.Pin_1, Q6.B
  N13: R4.Pin_0, Часть1.A4
  N14: R8.Pin_0, Часть1.A6
  N15: R8.Pin_1, Q1.B
  N16: R9.Pin_0, Часть1.A7
  N17: R9.Pin_1, Q4.B
  N18: R10.Pin_0, Q5.B
  N19: R10.Pin_1, Часть1.A0
  N20: R11.Pin_0, Q3.B
  N21: R11.Pin_1, Часть1.A1
  N22: R12.Pin_0, Часть1.D10
  N23: R13.Pin_0, Часть1.D9
  N24: R14.Pin_0, Часть1.D12/MISO
  N25: R15.Pin_0, Часть1.D8
  N26: R15.Pin_1, T9.Vout
  N27: R16.Pin_0, Часть1.D11/MOSI
  N28: R17.Pin_0, Часть1.D7
  N29: R18.Pin_0, Часть1.D6
  N30: R19.Pin_0, Часть1.D5
  N31: R21.Pin_0, Q2.B
  N32: R21.Pin_1, Часть1.A2
  N33: Часть2.TXD, Pad5.pad, Часть1.GND
  N34: Часть2.RXD, Часть1.3V3
  N35: Часть2.VCC, Часть1.D1/TX
  N36: Часть2.GND, Часть1.D0/RX
  N37: Pad6.pad, Часть1.VIN
