# Fritzing sketch board vm67 2 version (saved by Fritzing 0.9.3b)
circuit board: 5.08642cm x 6.52164cm

parts:
  T1 = LM35 Temperature Sensor [package="TO92 [THT]"]
  T4 = LM35 Temperature Sensor [package="TO92 [THT]"]
  T5 = LM35 Temperature Sensor [package="TO92 [THT]"]
  T6 = LM35 Temperature Sensor [package="TO92 [THT]"]
  T7 = LM35 Temperature Sensor [package="TO92 [THT]"]
  T8 = LM35 Temperature Sensor [package="TO92 [THT]"]
  T10 = LM35 Temperature Sensor [package="TO92 [THT]"]
  T11 = LM35 Temperature Sensor [package="TO92 [THT]"]
  R1 = Resistor [tolerance=±5% resistance=220 package=THT]
  R3 = Resistor [tolerance=±5% resistance=220 package=THT]
  R4 = Resistor [tolerance=±5% resistance=220 package=THT]
  R8 = Resistor [tolerance=±5% resistance=220 package=THT]
  R9 = Resistor [tolerance=±5% resistance=220 package=THT]
  R13 = Resistor [tolerance=±5% resistance=220 package=THT]
  R14 = Resistor [tolerance=±5% resistance=220 package=THT]
  R15 = Resistor [tolerance=±5% resistance=220 package=THT]
  R16 = Resistor [tolerance=±5% resistance=220 package=THT]
  R17 = Resistor [tolerance=±5% resistance=220 package=THT]
  R18 = Resistor [tolerance=±5% resistance=220 package=THT]
  R21 = Resistor [tolerance=±5% resistance=220 package=THT]
  Часть2 = Bluetooth HC-05 Macho
  Q1 = NPN-Transistor [package="TO92 [THT]"]
  Q2 = NPN-Transistor [package="TO92 [THT]"]
  Q4 = NPN-Transistor [package="TO92 [THT]"]
  Q6 = NPN-Transistor [package="TO92 [THT]"]
  T9 = LM35 Temperature Sensor [package="TO92 [THT]"]
  Pad6 = Pad [width=2.9430967356682807 height=2.3536616714875067 connect=center]
  Часть1 = Arduino Nano (Rev3.0)
  Pad4 = Pad [width=2.8581846161484794 height=2.6698012828151487 connect=center]
  Pad7 = Pad [width=3.0361206482524423 height=2.696848607461666 connect=center]
  R22 = Resistor [tolerance=±5% resistance=220 package=THT]
  T12 = LM35 Temperature Sensor [package="TO92 [THT]"]
  R25 = Resistor [tolerance=±5% resistance=220 package=THT]
  Pad5 = Pad [width=2.7067618098928712 height=2.1406198853588978 connect=center]

nets:
  N1: T1.Vout, R4.Pin_1
  GND: T1.GND, T4.GND, Часть2.RXD, Q1.C, Q2.C, Q4.C, Q6.C, Pad4.pad
  N2: T4.Vout, R1.Pin_1
  N3: T5.Vout, R13.Pin_1
  GND_2: T5.GND, T6.GND, T7.GND, T8.GND, T10.GND, T11.GND, T9.GND
  N4: T6.Vout, R14.Pin_1
  N5: T7.Vout, R16.Pin_1
  N6: T8.Vout, R17.Pin_1
  N7: T10.Vout, R18.Pin_1
  N8: T11.Vout, R22.Pin_1
  N9: R1.Pin_0, Часть1.D13/SCK
  N10: R3.Pin_0, Q6.B
  N11: R3.Pin_1, Часть1.A5
  N12: R4.Pin_0, Часть1.A4
  N13: R8.Pin_0, Q1.B
  N14: R8.Pin_1, Часть1.D3
  N15: R9.Pin_0, Часть1.D2
  N16: R9.Pin_1, Q4.B
  N17: R13.Pin_0, R15.Pin_0, Часть1.D7, Часть1.D8
  N18: R14.Pin_0, Часть1.D11/MOSI
  N19: R15.Pin_1, T9.Vout
  N20: R16.Pin_0, Часть1.D10
  N21: R17.Pin_0, R18.Pin_0, Часть1.D5, Часть1.D6
  N22: R21.Pin_0, Часть1.D12/MISO
  N23: R21.Pin_1, Q2.B
  N24: Часть2.TXD, Часть1.GND, Pad7.pad, Pad5.pad
  N25: Часть2.VCC, Часть1.D1/TX
  N26: Часть2.GND, Часть1.D0/RX
  N27: Pad6.pad, Часть1.VIN
  N28: Часть1.D4, R25.Pin_1
  N29: Часть1.D9, R22.Pin_0
  N30: T12.Vout, R25.Pin_0
