# Fritzing sketch schema vm45 (saved by Fritzing 0.9.3b)

parts:
  U1 = Vibration Motor- ROB-08449 [package=vibe-motor-10mm]
  Q1 = NPN-Transistor [package="TO92 [THT]"]
  U2 = Vibration Motor- ROB-08449 [package=vibe-motor-10mm]
  Q2 = NPN-Transistor [package="TO92 [THT]"]
  U3 = Vibration Motor- ROB-08449 [package=vibe-motor-10mm]
  Q3 = NPN-Transistor [package="TO92 [THT]"]
  U4 = Vibration Motor- ROB-08449 [package=vibe-motor-10mm]
  Q4 = NPN-Transistor [package="TO92 [THT]"]
  U5 = 74HC595 [package="DIP16 [THT]"]
  R1 = Resistor [tolerance=±5% resistance=220 package="0805 [SMD]"]  # not connected
  R2 = Resistor [tolerance=±5% resistance=220 package="0805 [SMD]"]  # not connected
  R3 = Resistor [tolerance=±5% resistance=220 package="0805 [SMD]"]  # not connected
  R4 = Resistor [tolerance=±5% resistance=220 package="0805 [SMD]"]  # not connected
  R5 = Resistor [tolerance=±5% resistance=220 package="0805 [SMD]"]  # not connected
  U6 = Vibration Motor- ROB-08449 [package=vibe-motor-10mm]
  Q5 = NPN-Transistor [package="SOT-23 [SMD]"]
  U7 = Vibration Motor- ROB-08449 [package=vibe-motor-10mm]
  U8 = Vibration Motor- ROB-08449 [package=vibe-motor-10mm]
  U9 = Vibration Motor- ROB-08449 [package=vibe-motor-10mm]
  U10 = Vibration Motor- ROB-08449 [package=vibe-motor-10mm]
  Q6 = NPN-Transistor [package="TO92 [THT]"]
  Q7 = NPN-Transistor [package="TO92 [THT]"]
  Q8 = NPN-Transistor [package="TO92 [THT]"]
  Q9 = NPN-Transistor [package="TO92 [THT]"]
  U11 = 74HC595 [package="DIP16 [THT]"]
  R6 = Resistor [tolerance=±5% resistance=220 package="0805 [SMD]"]  # not connected
  R7 = Resistor [tolerance=±5% resistance=220 package="0805 [SMD]"]  # not connected
  R8 = Resistor [tolerance=±5% resistance=220 package="0805 [SMD]"]  # not connected
  R9 = Resistor [tolerance=±5% resistance=220 package="0805 [SMD]"]  # not connected
  R10 = Resistor [tolerance=±5% resistance=220 package="0805 [SMD]"]  # not connected
  U12 = Vibration Motor- ROB-08449 [package=vibe-motor-10mm]
  Q10 = NPN-Transistor [package="SOT-23 [SMD]"]
  U13 = Vibration Motor- ROB-08449 [package=vibe-motor-10mm]
  U14 = Vibration Motor- ROB-08449 [package=vibe-motor-10mm]
  U15 = Vibration Motor- ROB-08449 [package=vibe-motor-10mm]
  U16 = Vibration Motor- ROB-08449 [package=vibe-motor-10mm]
  Q11 = NPN-Transistor [package="TO92 [THT]"]
  Q12 = NPN-Transistor [package="TO92 [THT]"]
  Q13 = NPN-Transistor [package="TO92 [THT]"]
  Q14 = NPN-Transistor [package="TO92 [THT]"]
  U17 = 74HC595 [package="DIP16 [THT]"]
  R11 = Resistor [tolerance=±5% resistance=220 package="0805 [SMD]"]  # not connected
  R12 = Resistor [tolerance=±5% resistance=220 package="0805 [SMD]"]  # not connected
  R13 = Resistor [tolerance=±5% resistance=220 package="0805 [SMD]"]  # not connected
  R14 = Resistor [tolerance=±5% resistance=220 package="0805 [SMD]"]  # not connected
  R15 = Resistor [tolerance=±5% resistance=220 package="0805 [SMD]"]  # not connected
  U18 = Vibration Motor- ROB-08449 [package=vibe-motor-10mm]
  Q15 = NPN-Transistor [package="SOT-23 [SMD]"]
  U19 = Vibration Motor- ROB-08449 [package=vibe-motor-10mm]
  U20 = Vibration Motor- ROB-08449 [package=vibe-motor-10mm]
  U21 = Vibration Motor- ROB-08449 [package=vibe-motor-10mm]
  U22 = Vibration Motor- ROB-08449 [package=vibe-motor-10mm]
  Q16 = NPN-Transistor [package="TO92 [THT]"]
  Q17 = NPN-Transistor [package="TO92 [THT]"]
  Q18 = NPN-Transistor [package="TO92 [THT]"]
  Q19 = NPN-Transistor [package="TO92 [THT]"]
  U23 = 74HC595 [package="DIP16 [THT]"]
  R16 = Resistor [tolerance=±5% resistance=220 package="0805 [SMD]"]  # not connected
  R17 = Resistor [tolerance=±5% resistance=220 package="0805 [SMD]"]  # not connected
  R18 = Resistor [tolerance=±5% resistance=220 package="0805 [SMD]"]  # not connected
  R19 = Resistor [tolerance=±5% resistance=220 package="0805 [SMD]"]  # not connected
  R20 = Resistor [tolerance=±5% resistance=220 package="0805 [SMD]"]  # not connected
  U24 = Vibration Motor- ROB-08449 [package=vibe-motor-10mm]
  Q20 = NPN-Transistor [package="SOT-23 [SMD]"]
  Часть1 = Arduino Uno (Rev3)
  Часть2 = Bluetooth HC-05 Macho
  R21 = Rotary Potentiometer (Large) [maximum_resistance=100kΩ package=THT]
  U25 = LIPO-110mAh [package=lipo-110]
  U26 = SWITCH_SPDT [package=kps-1290]
  U27 = SWITCH_SPDT [package=kps-1290]
  U29 = LIPO-2000mAh [package=lipo-2000]
  Grove1 = Grove OLED 128x96

nets:
  N1: U1.+, Q1.E
  N2: U2.+, Q2.E
  N3: U3.+, Q3.E
  N4: U4.+, Q4.E
  N5: U5.Q7', U11.DS
  N6: U5.SH_CP, U11.SH_CP, U17.SH_CP, U23.SH_CP, Часть1.D11_PWM/MOSI
  N7: U5.ST_CP, U11.ST_CP, U17.ST_CP, U23.ST_CP, Часть1.D12/MISO
  N8: U5.DS, Часть1.D13/SCK
  N9: U6.+, Q5.2
  N10: U7.+, Q9.E
  N11: U8.+, Q6.E
  N12: U9.+, Q8.E
  N13: U10.+, Q7.E
  N14: U11.Q7', U17.DS
  N15: U12.+, Q10.2
  N16: U13.+, Q13.E
  N17: U14.+, Q11.E
  N18: U15.+, Q12.E
  N19: U16.+, Q14.E
  N20: U17.Q7', U23.DS
  N21: U18.+, Q15.2
  N22: U19.+, Q18.E
  N23: U20.+, Q16.E
  N24: U21.+, Q17.E
  N25: U22.+, Q19.E
  N26: U24.+, Q20.2
  N27: U24.-, U26.O
  N28: Q20.1, U25.-
  N29: Часть1.A0, R21.wiper
  N30: Часть1.A4/SDA, Grove1.SDA
  N31: Часть1.A5/SCL, Grove1.SCL
  N32: Часть1.D9_PWM, Часть2.TXD
  N33: Часть1.D10_PWM/SS, Часть2.RXD
  3V3: Часть1.3V3, Часть2.VCC
  GND: Часть1.GND, Часть2.GND, U29.-
  N34: Часть1.VIN, U27.O
  N35: U25.+, U26.P
  N36: U27.P, U29.+
